// Logisim project One_bit_hack_alu.circ as structural Verilog: 1 circuit, main circuit main
module main (
  input  x,
  input  false1,
  input  nx,
  input  zx,
  input  no,
  input  f,
  input  y,
  input  false2,
  input  ny,
  input  zy,
  input  in_11,
  output out1,
  output zr,
  output ng
);

  wire adder_1_cout, adder_1_out, and_1_out, multiplexer_1_out, multiplexer_2_out, multiplexer_3_out,
       multiplexer_4_out, multiplexer_5_out, not_1_out, not_2_out, not_3_out, or_1_out;

  Multiplexer multiplexer_1 (.in0(x), .in1(false1), .out(multiplexer_1_out), .sel(zx));
  Multiplexer multiplexer_2 (.in0(y), .in1(false2), .out(multiplexer_2_out), .sel(zy));
  Multiplexer multiplexer_3 (.in0(multiplexer_1_out), .in1(not_1_out), .out(multiplexer_3_out), .sel(nx));
  not not_1 (not_1_out, multiplexer_1_out);
  Multiplexer multiplexer_4 (.in0(multiplexer_2_out), .in1(not_2_out), .out(multiplexer_4_out), .sel(ny));
  not not_2 (not_2_out, multiplexer_2_out);
  Adder #(.width(1)) adder_1 (
    .a(multiplexer_3_out), .b(multiplexer_4_out), .out(adder_1_out), .cout(adder_1_cout));  // open: cin
  and and_1 (and_1_out, multiplexer_3_out, multiplexer_4_out);
  Multiplexer multiplexer_5 (.in0(adder_1_out), .in1(and_1_out), .out(multiplexer_5_out), .sel(f));
  not not_3 (not_3_out, multiplexer_5_out);
  Multiplexer multiplexer_6 (.in0(multiplexer_5_out), .in1(not_3_out), .out(out1), .sel(no));
  not not_4 (zr, or_1_out);
  or or_1 (or_1_out, out1, out1);
  and and_2 (ng, out1, in_11);
endmodule
