// Logisim project Mux_Simulation.circ as structural Verilog: 1 circuit, main circuit main
module main (
  input  x,
  input  sel,
  input  y,
  output Mux
);

  wire and_1_out, and_2_out, not_1_out;

  not not_1 (not_1_out, sel);
  and and_1 (and_1_out, x, not_1_out);
  and and_2 (and_2_out, sel, y);
  or or_1 (Mux, and_1_out, and_2_out);
endmodule
