// Logisim project 4BitSISO.circ as structural Verilog: 1 circuit, main circuit main
module main (
  input  input1,
  input  reset,
  input  reset2,
  input  reset3,
  input  reset4,
  output out2
);

  wire a_q, b_q, c_q, clk_out;

  D_Flip_Flop a (.D(input1), .clk(clk_out), .Q(a_q), .reset(reset));  // open: Qn, preset
  Clock clk (.out(clk_out));
  D_Flip_Flop b (.D(a_q), .clk(clk_out), .Q(b_q), .reset(reset2));  // open: Qn, preset
  D_Flip_Flop c (.D(b_q), .clk(clk_out), .Q(c_q), .reset(reset3));  // open: Qn, preset
  D_Flip_Flop d (.D(c_q), .clk(clk_out), .Q(out2), .reset(reset4));  // open: Qn, preset
endmodule
