// Logisim project logisim_simulation.circ as structural Verilog: 1 circuit, main circuit main
module main (
  input  a,
  input  b,
  input  c,
  output sum,
  output carry
);

  wire and_1_out, and_2_out, or_1_out, xor_1_out, xor_2_out;

  xor xor_1 (xor_1_out, a, b);
  or or_1 (or_1_out, c, c);
  and and_1 (and_1_out, c, b);
  xor xor_2 (xor_2_out, c, b);
  xor xor_3 (sum, xor_1_out, or_1_out);
  and and_2 (and_2_out, xor_2_out, a);
  or or_2 (carry, and_1_out, and_2_out);
endmodule
